// Logisim project spaghetti.circ as structural Verilog: 1 circuit, main circuit main
module main (
  output [7:0] currentInstruction,
  output Subtract,
  output out_3,
  output out_4,
  output [1:0] ReadReg1,
  output [7:0] RegData1,
  output [1:0] WriteReg,
  output WriteEnable,
  output [7:0] RegDataW,
  output [1:0] ReadReg2,
  output [7:0] RegData2,
  output [7:0] RegData3,
  output [1:0] ReadReg3
);

  wire and_1_out, and_2_out, and_3_out, and_4_out, clock_1_out, decoder_1_out0, decoder_1_out1,
       decoder_1_out2, decoder_1_out3, not_1_out, not_2_out;
  wire [7:0] adder_1_out, adder_2_out, dataMemory_dout, multiplexer_5_out, PC_q, subtractor_1_out, X1_q,
       X2_q, X3_q, X4_q;

  Clock clock_1 (.out(clock_1_out));
  Adder adder_1 (.a(8'h1), .b(PC_q), .out(adder_1_out));  // open: cin, cout
  Decoder #(.select(2)) decoder_1 (
    .out0(decoder_1_out0), .out1(decoder_1_out1), .out2(decoder_1_out2), .out3(decoder_1_out3),
    .sel(currentInstruction[5:4]));  // open: en
  Register PC (.D(adder_1_out), .en(1'b1), .clk(clock_1_out), .Q(PC_q));  // open: clr
  Multiplexer #(.width(8)) multiplexer_1 (.in0(multiplexer_5_out), .in1(dataMemory_dout), .out(RegDataW), .sel(out_4));
  and and_1 (and_1_out, WriteEnable, decoder_1_out0);
  and and_2 (and_2_out, WriteEnable, decoder_1_out1);
  and and_3 (and_3_out, WriteEnable, decoder_1_out2);
  and and_4 (and_4_out, WriteEnable, decoder_1_out3);
  RAM #(.enables("line")) instructionMemory (
    .addr(PC_q), .we(1'b0), .oe(1'b1), .clk(clock_1_out), .dout(currentInstruction));  // open: din
  Register X1 (.D(RegDataW), .en(and_1_out), .clk(clock_1_out), .Q(X1_q));  // open: clr
  Register X2 (.D(RegDataW), .en(and_2_out), .clk(clock_1_out), .Q(X2_q));  // open: clr
  Register X3 (.D(RegDataW), .en(and_3_out), .clk(clock_1_out), .Q(X3_q));  // open: clr
  Register X4 (.D(RegDataW), .en(and_4_out), .clk(clock_1_out), .Q(X4_q));  // open: clr
  RAM #(.enables("line")) dataMemory (
    .addr(multiplexer_5_out), .we(out_3), .oe(1'b1), .clk(clock_1_out), .din(RegData3), .dout(dataMemory_dout));
  Multiplexer #(.select(2), .width(8)) multiplexer_2 (
    .in0(X1_q), .in1(X2_q), .in2(X3_q), .in3(X4_q), .out(RegData3), .sel(currentInstruction[5:4]));
  Multiplexer #(.select(2), .width(8)) multiplexer_3 (
    .in0(X1_q), .in1(X2_q), .in2(X3_q), .in3(X4_q), .out(RegData1), .sel(currentInstruction[3:2]));
  Multiplexer #(.select(2), .width(8)) multiplexer_4 (
    .in0(X1_q), .in1(X2_q), .in2(X3_q), .in3(X4_q), .out(RegData2), .sel(currentInstruction[1:0]));
  Adder adder_2 (.a(RegData1), .b(RegData2), .out(adder_2_out));  // open: cin, cout
  Multiplexer #(.width(8)) multiplexer_5 (
    .in0(adder_2_out), .in1(subtractor_1_out), .out(multiplexer_5_out), .sel(Subtract));
  not not_1 (not_1_out, currentInstruction[7]);
  not not_2 (not_2_out, currentInstruction[6]);
  and and_5 (Subtract, not_1_out, currentInstruction[6]);
  and and_6 (out_4, currentInstruction[7], not_2_out);
  Subtractor subtractor_1 (.a(RegData1), .b(RegData2), .out(subtractor_1_out));  // open: bin, bout
  and and_7 (out_3, currentInstruction[7], currentInstruction[6]);
  not not_3 (WriteEnable, out_3);

  assign ReadReg1 = currentInstruction[3:2];
  assign ReadReg2 = currentInstruction[1:0];
  assign ReadReg3 = currentInstruction[5:4];
  assign WriteReg = currentInstruction[5:4];

  // Notes on the sheet:
  //   Write Port
  //   Summer Jenssen
  //   I pledge my honor that I have abided by the Stevens Honor System
  //   Register File
  //   write
  //   Instruction Memory
  //   Data Memory
  //   read
  //   Read Port 1
  //   Read Port 2
  //   Rn
  //   Rt
  //   used when STR/LDr
  //   writeReg/ Rm
  //   this mux detects if you added or subtracted, sneding the apporpriate calc
  //   Problem: Can't store something to registers without storing it to memory first. Need to allow it to circumvent this.
  //   This checks if we are subtracting! If we are, we select the result from the ALU that came from sub to write back.
  //   ALU
  //   toggles writeEnable for data memory & registers
  //   Decides where to get data from when updating registers! If 1, get it from data memory. If 0, get it from ALU
  //   The only instruction that writes to data memory is 11, so !(11) is everything that writes to a register. 
  //   Unless you are using STR, shouldn't send data to data memory. 
endmodule
